# Fritzing sketch STMPE610 (saved by Fritzing 0.9.3b)
circuit board: 8.46667cm x 5.64444cm
breadboards: 1

parts:
  Part1 = Adafruit STMPE610 Breakout [part_number="Adafruit #1571"]
  Raspberry_Pi_1 = Raspberry Pi 3 [part_number=RPI-3-V1.2]

nets:
  +5V: Part1.+5V, Raspberry_Pi_1.3v3
  GND: Part1.GND, Raspberry_Pi_1.GND
  N1: Part1.SCL_5V, Raspberry_Pi_1.GPIO3
  N2: Part1.SDA_5V, Raspberry_Pi_1.GPIO2

custom parts:
  Adafruit STMPE610 Breakout: Getting touchy performance with your screen's touch screen? Resistive touch screens are incredibly popular as overlays to TFT and LCD displays. Only problem is they require a bunch of analog pins and you have to keep polling them since the overlays themselves are basically just big potentiometers. If your microcontroller doesn't have analog inputs, or maybe you want just a way more elegant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
